# Fritzing sketch KnobServo (saved by Fritzing 0.9.3b)
breadboards: 1

parts:
  Part1 = Arduino Uno (Rev3)
  U2 = POT [package=pot_alpha_rv16af-20]
  LED1 = LED - 5mm [color="Red (633nm)" package="5 mm [THT]"]
  R1 = Resistor [tolerance=±5% resistance=220 package="2512 [SMD]"]
  J1 = Basic Servo

nets:
  N1: Part1.A0, U2.S
  N2: Part1.D3_PWM, R1.Pin_1
  N3: Part1.D4, J1.pulse
  5V: Part1.5V, U2.A, J1.vcc
  GND: Part1.GND, U2.E, LED1.cathode, J1.gnd
  N4: LED1.anode, R1.Pin_0
