# Fritzing sketch RadarMusic (saved by Fritzing 0.9.3b)
breadboards: 1

parts:
  Part1 = Arduino Uno (Rev3)
  HC-SR04_Sensor_1 = HC-SR04 Ultrasonic Distance Sensor
  J1 = Piezo Speaker

nets:
  N1: Part1.D8, HC-SR04_Sensor_1.TRIG
  N2: Part1.D9_PWM, HC-SR04_Sensor_1.ECHO
  N3: Part1.D7, J1.pin2
  5V: Part1.5V, HC-SR04_Sensor_1.VCC
  GND: Part1.GND, HC-SR04_Sensor_1.GND, J1.pin1
