# Fritzing sketch LedSpeaker (saved by Fritzing 0.9.3b)
breadboards: 1

parts:
  Part1 = Arduino Uno (Rev3)
  J1 = Piezo Speaker
  LED1 = LED - 5mm [color="Red (633nm)" package="5 mm [THT]"]
  R1 = Resistor [tolerance=±5% resistance=220 package=THT]

nets:
  N1: Part1.D8, J1.pin2
  N2: Part1.GND, J1.pin1, LED1.cathode
  N3: Part1.D4, R1.Pin_1
  N4: LED1.anode, R1.Pin_0
