# Fritzing sketch ButtonNoPullup (saved by Fritzing 0.9.3b)
breadboards: 1

parts:
  Part1 = Arduino Uno (Rev3)
  LED1 = LED - 5mm [color="Red (633nm)" package="5 mm [THT]"]
  R1 = Resistor [tolerance=±5% resistance=220 package="2512 [SMD]"]
  S1 = Pushbutton [package="[THT]"]
  R2 = Resistor [tolerance=±5% resistance=220 package="2512 [SMD]"]

nets:
  N1: Part1.D3_PWM, S1.Pin_3, S1.Pin_4
  N2: Part1.D4, R1.Pin_1
  N3: Part1.5V, R2.Pin_1
  N4: Part1.GND, LED1.cathode
  N5: LED1.anode, R1.Pin_0
  N6: S1.Pin_1, S1.Pin_2, R2.Pin_0
