# Fritzing sketch ClimateSensor (saved by Fritzing 0.9.3b)
breadboards: 1

parts:
  Part1 = Arduino Uno (Rev3)
  DHT11_1 = DHT11 module

nets:
  N1: Part1.A0, DHT11_1.DATA
  5V: Part1.5V, DHT11_1.VCC
  GND: Part1.GND, DHT11_1.GND

custom parts:
  DHT11 module: DHT11 black pcb module
